# Fritzing sketch RGBLED (saved by Fritzing 0.9.3b)
breadboards: 1

parts:
  부품1 = Arduino Uno (Rev3)
  LED1 = RGB LED (com. cathode, rgb) [package="5 mm [THT]"]
  R1 = Resistor [tolerance=±5% resistance=220 package=THT]
  R2 = Resistor [tolerance=±5% resistance=220 package=THT]
  R3 = Resistor [tolerance=±5% resistance=220 package=THT]

nets:
  N1: 부품1.D9_PWM, R1.Pin_0
  N2: 부품1.D10_PWM/SS, R2.Pin_0
  N3: 부품1.D11_PWM/MOSI, R3.Pin_0
  N4: 부품1.GND, LED1.blue_anode
  N5: LED1.red_anode, R1.Pin_1
  N6: LED1.common_cathode, R2.Pin_1
  N7: LED1.green_anode, R3.Pin_1

// code stored in the sketch: RGB_LED_MODULE_TEST.ino
/*
1? ???? RGB_LED? ???? ?????.
??? ?? : SZH-EK058
*/
const int ledred = 11;
const int ledgreen = 10;
const int ledblue = 9;

void setColor(int red,int green,int blue){
  analogWrite(ledred,red);
  analogWrite(ledgreen,green);
  analogWrite(ledblue,blue);  
}

void setup(){
  pinMode(ledred,OUTPUT);
  pinMode(ledgreen,OUTPUT);
  pinMode(ledblue,OUTPUT);
}

void loop(){
  setColor(255,0,0); //Red
  delay(1000);
	setColor(255,153,0); //Orange
  delay(1000);
	setColor(255,255,0); //Yellow
  delay(1000);
	setColor(0,255,0); //Green
  delay(1000);
	setColor(0,0,255); //Blue
  delay(1000);
	setColor(0,0,102); //Navy
  delay(1000);
	setColor(02,0,153); //Purple
  delay(1000);
}

// code stored in the sketch: Untitled2.ino
Red (255,0,0) //FF0000
Orange (255,153,0) //FF9900
Yellow (255,255,0) //FFFF00
Green (0,255,0) //00FF00
Blue (0,0,255) //0000FF
Navy (0,0,102) //000066
Purple (102,0,153) //660099
