# Fritzing sketch example01 (saved by Fritzing 0.9.0b)
breadboards: 1

parts:
  부품1 = Arduino Uno (Rev3) - ICSP
  R1 = Resistor [tolerance=±1% resistance=220 package=THT]
  LED1 = LED - 5mm [color="Green (570nm)" package="5 mm [THT]"]

nets:
  N1: 부품1.D7, R1.Pin_1
  N2: 부품1.GND, LED1.cathode
  N3: R1.Pin_0, LED1.anode
