# Fritzing sketch example02 (saved by Fritzing 0.9.0b)
breadboards: 1

parts:
  부품1 = Arduino Uno (Rev3)
  LED1 = LED - 5mm [color="Red (633nm)" package="5 mm [THT]"]
  S1 = Pushbutton [package="[THT]"]
  R1 = Resistor [tolerance=±5% resistance=220 package=THT]
  R2 = Resistor [tolerance=±5% resistance=220 package=THT]
  R3 = Resistor [tolerance=±5% resistance=220 package=THT]
  R4 = Resistor [tolerance=±5% resistance=220 package=THT]
  LED2 = LED - 5mm [color="Red (633nm)" package="5 mm [THT]"]
  LED3 = LED - 5mm [color="Red (633nm)" package="5 mm [THT]"]
  R5 = Resistor [tolerance=±5% resistance=220 package=THT]  # not connected

nets:
  N1: 부품1.D11_PWM/MOSI, R4.Pin_1
  N2: 부품1.D12/MISO, R3.Pin_1
  N3: 부품1.D13/SCK, R2.Pin_1
  N4: 부품1.GND, LED1.cathode, R1.Pin_1, LED2.cathode, LED3.cathode
  N5: 부품1.D2, S1.Pin_1, S1.Pin_2
  N6: 부품1.5V, S1.Pin_3, S1.Pin_4, R1.Pin_0
  N7: LED1.anode, R2.Pin_0
  N8: R3.Pin_0, LED2.anode
  N9: R4.Pin_0, LED3.anode
